# Fritzing sketch schematic-base (saved by Fritzing 0.9.3b)

parts:
  MH-ET_LIVE_ESP32_DEVKIT1 = MH-ET LIVE ESP32 DEVKIT 38 pins
  M1 = Osoyoo SX1278-ra-02
  ZS-042_RTC1 = ZS-042 RTC Module

nets:
  3V3: MH-ET_LIVE_ESP32_DEVKIT1.3V3, M1.3.3V, ZS-042_RTC1.VCC
  GND: MH-ET_LIVE_ESP32_DEVKIT1.GND, M1.GND, ZS-042_RTC1.GND
  N1: MH-ET_LIVE_ESP32_DEVKIT1.IO23, M1.MOSI
  N2: MH-ET_LIVE_ESP32_DEVKIT1.IO22, ZS-042_RTC1.SCL
  N3: MH-ET_LIVE_ESP32_DEVKIT1.IO21, ZS-042_RTC1.SDA
  N4: MH-ET_LIVE_ESP32_DEVKIT1.IO19, M1.MISO
  N5: MH-ET_LIVE_ESP32_DEVKIT1.IO18, M1.SCK
  N6: MH-ET_LIVE_ESP32_DEVKIT1.IO5, M1.NSS
  N7: MH-ET_LIVE_ESP32_DEVKIT1.IO4, M1.RST
  N8: MH-ET_LIVE_ESP32_DEVKIT1.IO2, M1.DIO0

custom parts:
  MH-ET LIVE ESP32 DEVKIT 38 pins: http://mh.nodebb.com/topic/2/mh-et-live-esp32-devkit
  Osoyoo SX1278-ra-02: Osoyoo Long Distance wireless transceiver Uart LoRa Module.
